# Fritzing sketch branchement_lcd (saved by Fritzing 0.9.9b)
breadboards: 1

parts:
  Part3 = Arduino Mega 2560 (Rev3)
  LCD2 = LCD screen

nets:
  GND: Part3.GND, LCD2.VSS, LCD2.LED-
  5V: Part3.5V, LCD2.VDD, LCD2.LED+
  N1: Part3.D26, LCD2.DB7
  N2: Part3.D28, LCD2.DB6
  N3: Part3.D30, LCD2.DB5
  N4: Part3.D32, LCD2.DB4
  N5: Part3.D34, LCD2.E
  N6: Part3.D36, LCD2.RS
  N7: Part3.D38, LCD2.V0
